# Fritzing sketch myPcb (saved by Fritzing 0.9.3b)
circuit board: 4.74286cm x 4.69786cm
circuit board: 6.76948cm x 5.35518cm
breadboards: 1

parts:
  J1 = AVR ISP 6 Pin [package=2x3]
  SparkFun_Particle_Sensor_Breakout_-_MAX1 = SparkFun MAX30105_Breakout [part_number=SEN-14045]

nets:
  N1: J1.2, SparkFun_Particle_Sensor_Breakout_-_MAX1.5V
  N2: J1.3, SparkFun_Particle_Sensor_Breakout_-_MAX1.SDA
  N3: J1.5, SparkFun_Particle_Sensor_Breakout_-_MAX1.SCL
  N4: J1.6, SparkFun_Particle_Sensor_Breakout_-_MAX1.GND

custom parts:
  SparkFun MAX30105_Breakout: Description: The SparkFun MAX30105 Particle Sensor is a flexible, powerful sensor enabling sensing of distance, heart rate, particle detection and even the blinking of an eye. The MAX30105 has been equipped with three LEDs as well as a very sensitive photon detector. The idea is to pulse the different LEDs, then detect what shines back. Based on the reflected signature it’s possible to detect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
